# Fritzing sketch AutoCurtains (saved by Fritzing 0.9.10b)
breadboards: 1

parts:
  MCU1 = Raspberry Pi Zero
  Pololu_A1 = Pololu A4988 [package=SO16]
  C1 = Electrolytic Capacitor [capacitance=100μF voltage=35V package="0807 [SMD, electrolytic]"]
  IC1 = Voltage Regulator [package=78xxl]
  J1 = Power Jack [package=power_jack_combo]
  M1 = Stepper Motor - Bipolar

nets:
  N1: MCU1.pin_3, Pololu_A1.DIR
  N2: MCU1.pin_4, Pololu_A1.VDD, IC1.OUT
  GND: MCU1.pin_6, MCU1.pin_39, Pololu_A1.GND, C1.-, IC1.GND, J1.GND
  N3: MCU1.pin_27, Pololu_A1.ENABLE
  N4: MCU1.pin_28, Pololu_A1.STEP
  N5: Pololu_A1.RESET, Pololu_A1.SLEEP
  N6: Pololu_A1.1B, M1.D
  N7: Pololu_A1.1A, M1.B
  N8: Pololu_A1.2A, M1.C
  N9: Pololu_A1.2B, M1.A
  N10: Pololu_A1.VMOT, C1.+, IC1.IN, J1.PWR

notes:
  AutoCurtains, A
